# Fritzing sketch iot-switch (saved by Fritzing 0.9.3b)

parts:
  Arduino = Arduino Nano (Rev3.0)
  WiFi = ESP8266 WiFi Module [part_number=ESP8266]
  R1 = Resistor [tolerance=±5% resistance=220 package=THT]
  R2 = Resistor [tolerance=±5% resistance=220 package=THT]
  Connection = LED - 5mm [color="Red (633nm)" package="5 mm [THT]"]
  Output = LED - 5mm [color="Red (633nm)" package="5 mm [THT]"]
  Reset = Pushbutton [package="[THT]"]
  Mode = Toggle Switch [package=THT]
  Earase = Pushbutton [package="[THT]"]

nets:
  N1: Arduino.GND, R1.Pin_1, R2.Pin_1, Reset.Pin_1, Reset.Pin_2, Mode.COM, Earase.Pin_3, Earase.Pin_4
  N2: Arduino.D2, WiFi.TXD
  N3: Arduino.D3, WiFi.RXD
  N4: Arduino.D4, Mode.L1
  3V3: Arduino.3V3, WiFi.VCC, WiFi.CH_PD
  N5: WiFi.GPIO_0, Connection.cathode, Earase.Pin_1, Earase.Pin_2
  N6: WiFi.GPIO_2, Output.cathode
  N7: WiFi.REST, Reset.Pin_3, Reset.Pin_4
  N8: R1.Pin_0, Connection.anode
  N9: R2.Pin_0, Output.anode
